// Logisim project ex4.circ as structural Verilog: 1 circuit, main circuit main
module main (
  input  A,
  input  B,
  output RESULT
);

  wire not_1_out;

  not not_1 (not_1_out, A);
  and and_1 (RESULT, not_1_out, B);
endmodule
