// Logisim project ex5v6.circ as structural Verilog: 1 circuit, main circuit main
module main (
  input  D1,
  input  D2,
  input  D3,
  input  D4
);

  wire nand_1_out, nand_2_out, nand_3_out, nand_4_out, nand_5_out, nand_6_out, nand_7_out, nand_8_out,
       nand_9_out, nand_10_out, nand_11_out, nand_12_out, nand_13_out, nand_14_out, nand_15_out, nand_16_out,
       nand_17_out, nand_18_out, nand_19_out, nand_20_out, not_1_out, not_2_out, not_3_out, not_4_out,
       not_5_out, not_6_out, not_7_out, not_8_out, not_9_out, not_10_out;

  not not_1 (not_1_out, D1);
  not not_2 (not_2_out, D2);
  not not_3 (not_3_out, D3);
  not not_4 (not_4_out, D4);
  nand nand_1 (nand_1_out, not_2_out, not_1_out, D4, not_3_out);
  nand nand_2 (nand_2_out, D2, not_3_out, not_4_out);
  nand nand_3 (nand_3_out, D4, D2, not_3_out);
  nand nand_4 (nand_4_out, D2, not_4_out, D3);
  nand nand_5 (nand_5_out, not_2_out, not_4_out, D3);
  nand nand_6 (nand_6_out, not_1_out, not_3_out, not_2_out, D4);
  nand nand_7 (nand_7_out, D2, not_4_out, not_3_out);
  nand nand_8 (nand_8_out, D3, D2, D4);
  nand nand_9 (nand_9_out, D2, not_3_out);
  nand nand_10 (nand_10_out, not_2_out, D3);
  nand nand_11 (nand_11_out, D3, D4);
  nand nand_12 (nand_12_out, not_1_out, not_2_out, D4);
  nand nand_13 (nand_13_out, not_1_out, not_2_out, not_3_out);
  nand nand_14 (nand_14_out, D2, D3, D4);
  nand nand_15 (nand_15_out, nand_1_out, nand_2_out);
  nand nand_16 (nand_16_out, nand_3_out, nand_4_out);
  nand nand_17 (nand_17_out, nand_6_out, nand_7_out, nand_8_out);
  nand nand_18 (nand_18_out, not_4_out, nand_9_out);
  nand nand_19 (nand_19_out, nand_10_out, nand_11_out, nand_12_out);
  nand nand_20 (nand_20_out, nand_13_out, nand_14_out);
  not not_5 (not_5_out, nand_15_out);
  not not_6 (not_6_out, nand_16_out);
  not not_7 (not_7_out, nand_17_out);
  not not_8 (not_8_out, nand_18_out);
  not not_9 (not_9_out, nand_19_out);
  not not_10 (not_10_out, nand_20_out);
  _7_Segment_Display u_7_segment_display_1 (
    .g(not_10_out), .f(not_9_out), .a(not_5_out), .b(not_6_out), .e(not_8_out), .d(not_7_out), .c(nand_5_out));  // open: dp
endmodule
